// Logisim project LAB1Q3.circ as structural Verilog: 1 circuit, main circuit main
module main (
  input  in_1,
  input  in_2,
  input  in_3,
  input  A,
  input  B,
  input  X,
  output out_7,
  output F_A__B__X
);

  wire and_1_out, and_2_out, not_1_out;

  not not_1 (not_1_out, X);
  Multiplexer #(.enable("false")) multiplexer_1 (.in0(in_1), .in1(in_2), .out(out_7), .sel(in_3));
  and and_1 (and_1_out, A, not_1_out);
  and and_2 (and_2_out, B, X);
  or or_1 (F_A__B__X, and_1_out, and_2_out);
endmodule
