// Logisim project LAB3.circ as structural Verilog
module HalfAdder (
  input  A,
  input  B,
  output S,
  output C
);

  xor xor_1 (S, A, B);
  and and_1 (C, A, B);
endmodule

module FullAdder (
  input  Cin,
  input  A,
  input  B,
  output sout,
  output cout
);

  wire halfadder_1_c, halfadder_1_s, halfadder_2_c;

  HalfAdder halfadder_1 (.A(A), .B(B), .S(halfadder_1_s), .C(halfadder_1_c));
  HalfAdder halfadder_2 (.A(Cin), .B(halfadder_1_s), .S(sout), .C(halfadder_2_c));
  or or_1 (cout, halfadder_2_c, halfadder_1_c);
endmodule

// ALU
module Alu (
  input  Sub,
  input  cin,
  input  A,
  input  B,
  input  [2:0] \function ,
  input  Less,
  output cout,
  output set,
  output result
);

  wire AND_out, negator_1_out, NOT_out, OR_out, xor_1_out, xor_2_out;

  xor xor_1 (xor_1_out, B, Sub);
  Adder #(.width(1)) adder_1 (.a(A), .b(xor_1_out), .out(set), .cin(cin), .cout(cout));
  Negator #(.width(1)) negator_1 (.in(A), .out(negator_1_out));
  or OR (OR_out, A, B);
  and AND (AND_out, A, B);
  not NOT (NOT_out, A);
  xor xor_2 (xor_2_out, A, B);
  Multiplexer #(.select(3), .enable("false")) multiplexer_1 (
    .in0(set), .in1(negator_1_out), .in2(OR_out), .in3(AND_out), .in4(NOT_out), .in5(xor_2_out), .in6(Less),
    .out(result), .sel(\function ));  // open: in7
endmodule

// ALU
module _8BitAlu (
  input  [7:0] A,
  input  Sub,
  input  [2:0] Op,
  input  [7:0] B,
  output [7:0] R,
  output N,
  output Z,
  output cout,
  output V
);

  wire alu_1_cout, alu_2_cout, alu_3_cout, alu_4_cout, alu_5_cout, alu_6_cout, alu_7_cout, alu_8_set;

  Alu alu_1 (
    .Sub(Sub), .cin(Sub), .A(A[0]), .B(B[0]), .Less(alu_8_set), .result(R[0]), .cout(alu_1_cout),
    .\function (Op));  // open: set
  Alu alu_2 (
    .Sub(Sub), .cin(alu_1_cout), .A(A[1]), .B(B[1]), .Less(1'b0), .result(R[1]), .cout(alu_2_cout),
    .\function (Op));  // open: set
  Alu alu_3 (
    .Sub(Sub), .cin(alu_2_cout), .A(A[2]), .B(B[2]), .Less(1'b0), .result(R[2]), .cout(alu_3_cout),
    .\function (Op));  // open: set
  Alu alu_4 (
    .Sub(Sub), .cin(alu_3_cout), .A(A[3]), .B(B[3]), .Less(1'b0), .result(R[3]), .cout(alu_4_cout),
    .\function (Op));  // open: set
  Alu alu_5 (
    .Sub(Sub), .cin(alu_4_cout), .A(A[4]), .B(B[4]), .Less(1'b0), .result(R[4]), .cout(alu_5_cout),
    .\function (Op));  // open: set
  Alu alu_6 (
    .Sub(Sub), .cin(alu_5_cout), .A(A[5]), .B(B[5]), .Less(1'b0), .result(R[5]), .cout(alu_6_cout),
    .\function (Op));  // open: set
  Alu alu_7 (
    .Sub(Sub), .cin(alu_6_cout), .A(A[6]), .B(B[6]), .Less(1'b0), .result(R[6]), .cout(alu_7_cout),
    .\function (Op));  // open: set
  Alu alu_8 (
    .Sub(Sub), .cin(alu_7_cout), .A(A[7]), .B(B[7]), .Less(1'b0), .set(alu_8_set), .result(N), .cout(cout),
    .\function (Op));
  nor nor_1 (Z, N, R[6], R[5], R[4], R[3], R[2], R[1], R[0]);
  xor xor_1 (V, alu_7_cout, cout);

  assign R[7] = N;
endmodule

// UV
module UpdatedFlags (
  input  [2:0] in_1,
  output UV,
  output out_3,
  output UN,
  output UZ
);

  wire ABC_out, ABNOT_C_out, ACNOT_B_out, ANOT_BC_out, not_1_out, not_2_out, not_3_out, NOT_A_BC_out,
       NOT_AB_C_out, NOT_ABC_out, NOT_AC_B_out;

  not not_1 (not_1_out, in_1[2]);
  not not_2 (not_2_out, in_1[1]);
  not not_3 (not_3_out, in_1[0]);
  and NOT_ABC (NOT_ABC_out, not_1_out, not_2_out, not_3_out);
  and NOT_AB_C (NOT_AB_C_out, not_1_out, not_2_out, in_1[0]);
  and NOT_AC_B (NOT_AC_B_out, not_1_out, in_1[1], not_3_out);
  and NOT_A_BC (NOT_A_BC_out, not_1_out, in_1[1], in_1[0]);
  and ANOT_BC (ANOT_BC_out, in_1[2], not_2_out, not_3_out);
  and ACNOT_B (ACNOT_B_out, in_1[2], not_2_out, in_1[0]);
  and ABNOT_C (ABNOT_C_out, in_1[2], in_1[1], not_3_out);
  and ABC (ABC_out, in_1[2], in_1[1], in_1[0]);
  or or_1 (UN, NOT_ABC_out, NOT_AB_C_out, NOT_AC_B_out, NOT_A_BC_out, ANOT_BC_out, ACNOT_B_out, ABNOT_C_out, ABC_out);
  or or_2 (out_3, ABNOT_C_out, NOT_AB_C_out, NOT_ABC_out);

  assign UV = out_3;
  assign UZ = UN;
endmodule

module calc (
  input  [7:0] InputA
);

  Register register_1 ();  // open: D, en, Q, clk, clr
  _8BitAlu u_8bitalu_1 ();  // open: A, B, Sub, Op, R, N, Z, cout, V
endmodule

module Test (
  input  [7:0] Input,
  input  A,
  input  B,
  input  A_2,
  input  [7:0] Input_2,
  input  B_2,
  input  C,
  output [7:0] out_8,
  output [7:0] \output ,
  output D
);

  Register Register (.D(Input), .en(A), .Q(out_8), .clr(B));  // open: clk
  Counter counter_1 (.load(A_2), .D(Input_2), .count(B_2), .Q(\output ), .carry(D), .clk(C));  // open: clr
endmodule
