// Logisim project Lab1Q1.circ as structural Verilog: 1 circuit, main circuit main
module main (
  input  A,
  input  B,
  output F_A__B,
  output out_4
);

  wire and_1_out, and_2_out, not_1_out, not_2_out;

  not not_1 (not_1_out, A);
  not not_2 (not_2_out, B);
  and and_1 (and_1_out, not_1_out, B);
  and and_2 (and_2_out, A, not_2_out);
  xor xor_1 (out_4, A, B);
  or or_1 (F_A__B, and_1_out, and_2_out);
endmodule
